// Logisim project Tic-Tac-Toe.circ as structural Verilog: 1 circuit, main circuit main
module main (
);

  wire button_1_out, cdm_8_1_p2, cdm_8_1_p4, cdm_8_1_p5, cdm_8_1_p6, cdm_8_1_p7, cdm_8_1_p8, cdm_8_1_p9,
       cdm_8_1_p10, cdm_8_1_p11, cl, code, data, not_1_out, rd_rw;
  wire [7:0] cdm_8_1_p13, cdm_8_1_p14, cdm_8_1_p15, controlled_buffer_1_out;

  // Probe on cdm_8_1_p2
  // Probe on cdm_8_1_p4
  Button button_1 (.out(button_1_out));
  Clock clock_1 (.out(cl));
  DotMatrix #(.matrixcols(9), .matrixrows(9)) dotmatrix_1 (
    .col0(9'h101), .col1(9'h82), .col2(9'h44), .col3(9'h28), .col4(9'h10), .col5(9'h28), .col6(9'h44),
    .col7(9'h82), .col8(9'h101));
  DotMatrix #(.matrixcols(9), .matrixrows(9)) dotmatrix_2 (
    .col0(9'h101), .col1(9'h82), .col2(9'h44), .col3(9'h28), .col4(9'h10), .col5(9'h28), .col6(9'h44),
    .col7(9'h82), .col8(9'h101));
  DotMatrix #(.matrixcols(9), .matrixrows(9)) dotmatrix_3 (
    .col0(9'h101), .col1(9'h82), .col2(9'h44), .col3(9'h28), .col4(9'h10), .col5(9'h28), .col6(9'h44),
    .col7(9'h82), .col8(9'h101));
  // Probe on cdm_8_1_p6
  // Probe on cdm_8_1_p5
  // Probe on cdm_8_1_p7
  DotMatrix #(.matrixcols(9), .matrixrows(9)) dotmatrix_4 (
    .col0(9'h101), .col1(9'h82), .col2(9'h44), .col3(9'h28), .col4(9'h10), .col5(9'h28), .col6(9'h44),
    .col7(9'h82), .col8(9'h101));
  DotMatrix #(.matrixcols(9), .matrixrows(9)) dotmatrix_5 (
    .col0(9'h101), .col1(9'h82), .col2(9'h44), .col3(9'h28), .col4(9'h10), .col5(9'h28), .col6(9'h44),
    .col7(9'h82), .col8(9'h101));
  DotMatrix #(.matrixcols(9), .matrixrows(9)) dotmatrix_6 (
    .col0(9'h101), .col1(9'h82), .col2(9'h44), .col3(9'h28), .col4(9'h10), .col5(9'h28), .col6(9'h44),
    .col7(9'h82), .col8(9'h101));
  // Probe on cdm_8_1_p8
  // Probe on cdm_8_1_p9
  Decoder #(.disabled(0)) decoder_1 (.out0(code), .out1(data), .sel(cdm_8_1_p10), .en(cdm_8_1_p11));
  assign controlled_buffer_1_out = not_1_out ? cdm_8_1_p14 : 8'bz;  // Controlled_Buffer controlled_buffer_1
  // CdM_8 cdm_8_1: pin names not known; wires that end beside it: cl, cdm_8_1_p2, button_1_out, cdm_8_1_p4, cdm_8_1_p5, cdm_8_1_p6, cdm_8_1_p7, cdm_8_1_p8, cdm_8_1_p9, cdm_8_1_p10, cdm_8_1_p11, rd_rw, cdm_8_1_p13, cdm_8_1_p14, cdm_8_1_p15
  not not_1 (not_1_out, rd_rw);
  assign cdm_8_1_p15 = rd_rw ? controlled_buffer_1_out : 8'bz;  // Controlled_Buffer controlled_buffer_2
  DotMatrix #(.matrixcols(9), .matrixrows(9)) dotmatrix_7 (
    .col0(9'h101), .col1(9'h82), .col2(9'h44), .col3(9'h28), .col4(9'h10), .col5(9'h28), .col6(9'h44),
    .col7(9'h82), .col8(9'h101));
  DotMatrix #(.matrixcols(9), .matrixrows(9)) dotmatrix_8 (
    .col0(9'hfe), .col1(9'h101), .col2(9'h101), .col3(9'h101), .col4(9'h101), .col5(9'h101), .col6(9'h101),
    .col7(9'h101), .col8(9'hfe));
  DotMatrix #(.matrixcols(9), .matrixrows(9)) dotmatrix_9 (
    .col0(9'h101), .col1(9'h82), .col2(9'h44), .col3(9'h28), .col4(9'h10), .col5(9'h28), .col6(9'h44),
    .col7(9'h82), .col8(9'h101));
  ROM rom_1 (.addr(cdm_8_1_p13), .data(controlled_buffer_1_out), .sel(code));
  RAM ram_1 (.addr(cdm_8_1_p13), .data(controlled_buffer_1_out), .sel(data), .clk(cl), .ld(rd_rw));  // open: clr

  // Notes on the sheet:
  //   contents of rom_1 (hex, n*v repeats v):
  //   d0 0 b0 d1 1 b5 14 d3 2 ac d4
  //   X figure
endmodule
